# Fritzing sketch poke_wiring (saved by Fritzing 0.8.7b)
breadboards: 1

parts:
  UNO = Arduino Uno (Rev3)
  R1 = Resistor [tolerance=±5% resistance=220 package=THT]
  PIEZO_BUZZER = Piezo Speaker
  COLOR_LED = LED - 5mm [color="White (4500K)" package="5 mm [THT]"]
  R3 = Resistor [tolerance=±5% resistance=47 package=THT]
  R4 = Resistor [tolerance=±5% resistance=47 package=THT]
  INFRARED_LED = LED - 5mm [color="Infrared (850nm)" package="5 mm [THT]"]
  R5 = Resistor [tolerance=±5% resistance=47 package=THT]
  R6 = Resistor [tolerance=±5% resistance=47 package=THT]
  INFRARED_PHOTODIODE = S1133 Si Photodiode [package="8mm Ceramic [THT]"]
  R7 = Resistor [tolerance=±5% resistance=100k package=THT]

nets:
  N1: UNO.D8, PIEZO_BUZZER.pin1
  N2: UNO.D10_PWM/SS, R1.Pin_0
  N3: UNO.D11_PWM/MOSI, R3.Pin_0
  N4: UNO.D7, INFRARED_PHOTODIODE.cathode, R7.Pin_1
  N5: UNO.5V, R5.Pin_0
  N6: UNO.GND, PIEZO_BUZZER.pin2, COLOR_LED.cathode, INFRARED_LED.cathode, R7.Pin_0
  N7: R1.Pin_1, COLOR_LED.anode
  N8: R3.Pin_1, R4.Pin_0
  N9: R4.Pin_1, INFRARED_LED.anode
  N10: R5.Pin_1, R6.Pin_0
  N11: R6.Pin_1, INFRARED_PHOTODIODE.anode
